# Fritzing sketch Arduino単独システム例 (saved by Fritzing 0.9.2b)
perfboards: 3

parts:
  パーツ1 = Arduino Uno (Rev3)  # not connected
  Pro_Mini_3V3_8MHz1 = Arduino Pro Mini v13
  S2 = Akizuki slide switch IS-1250
  Power_plug6 = Power plug
  J97 = Arduino R3 6pin male header [package=THT]  # not connected
  Reset1 = Momentary Switch [package=ksa_sealed_tac_switch]
  IOH2 = female pin header, 10 pins [form="♀ (female)"]
  Power2 = female pin header, 8 pins [form="♀ (female)"]
  IOL2 = female pin header, 8 pins [form="♀ (female)"]
  AD2 = female pin header, 6 pins [form="♀ (female)"]
  RTC3 = RTC-8564NB [package="Module(DIP 8P)"]
  S3 = Akizuki slide switch IS-1250
  J104 = Arduino R3 6pin male header [package=THT]  # not connected
  D7 = Schottky Diode [part_number=1N5817 package="300 mil [THT]"]
  D8 = Schottky Diode [part_number=1N5817 package="300 mil [THT]"]
  IOH4 = female pin header, 10 pins [form="♀ (female)"]
  INT2 = male pin header, 15 pins [form="♂ (male)"]
  J105 = male pin header, 15 pins [form="♂ (male)"]
  IOL4 = female pin header, 8 pins [form="♀ (female)"]
  Power4 = female pin header, 8 pins [form="♀ (female)"]
  AD4 = female pin header, 6 pins [form="♀ (female)"]
  BAT3 = Battery Holders [package=battcom_20mm_pth]
  Grove1 = Grove 3 Axis Digital Accelerometer 16g  # not connected
  パーツ5 = Arduino MicroSD Shield  # not connected
  Grove2 = Grove Infrared Emitter  # not connected
  Grove3 = Grove 3 Axis Digital Accelerometer 16g  # not connected
  VCC1 = Battery block 9V  # not connected
  Xbee3 = SSCI-KIT-XBSOCKET
  J110 = Arduino R3 6pin male header [package=THT]  # not connected
  IOH6 = female pin header, 10 pins [form="♀ (female)"]
  J111 = male pin header, 11 pins [form="♂ (male)"]
  Sleep1 = male pin header, 11 pins [form="♂ (male)"]
  Rx4 = male pin header, 15 pins [form="♂ (male)"]
  J112 = male pin header, 15 pins [form="♂ (male)"]
  Tx4 = male pin header, 15 pins [form="♂ (male)"]
  J113 = male pin header, 15 pins [form="♂ (male)"]
  INT3 = male pin header, 15 pins [form="♂ (male)"]
  J114 = male pin header, 15 pins [form="♂ (male)"]
  IOL6 = female pin header, 8 pins [form="♀ (female)"]
  Power6 = female pin header, 8 pins [form="♀ (female)"]
  AD6 = female pin header, 6 pins [form="♀ (female)"]  # not connected

nets:
  N1: Pro_Mini_3V3_8MHz1.D0/TX, IOL2.pin8
  N2: Pro_Mini_3V3_8MHz1.D1/RX, IOL2.pin7
  N3: Pro_Mini_3V3_8MHz1.VCC, S2.pin1, S2.pin4
  GND: Pro_Mini_3V3_8MHz1.GND, Power_plug6.GND, Reset1.4, IOH2.pin4, Power2.pin6, Power2.pin7
  N4: Pro_Mini_3V3_8MHz1.A4, AD2.pin5
  N5: Pro_Mini_3V3_8MHz1.A5, AD2.pin6
  N6: Pro_Mini_3V3_8MHz1.RAW, Power_plug6.VCC, Power2.pin8
  N7: Pro_Mini_3V3_8MHz1.RESET, Reset1.2, Power2.pin3
  N8: Pro_Mini_3V3_8MHz1.A3, AD2.pin4
  N9: Pro_Mini_3V3_8MHz1.A2, AD2.pin3
  N10: Pro_Mini_3V3_8MHz1.A1, AD2.pin2
  N11: Pro_Mini_3V3_8MHz1.A0, AD2.pin1
  N12: Pro_Mini_3V3_8MHz1.D13/SCK, IOH2.pin5
  N13: Pro_Mini_3V3_8MHz1.D12/MISO, IOH2.pin6
  N14: Pro_Mini_3V3_8MHz1.D11_PWM/MOSI, IOH2.pin7
  N15: Pro_Mini_3V3_8MHz1.D10_PWM/SS, IOH2.pin8
  N16: Pro_Mini_3V3_8MHz1.D9_PWM, IOH2.pin9
  N17: Pro_Mini_3V3_8MHz1.D8, IOH2.pin10
  N18: Pro_Mini_3V3_8MHz1.D7, IOL2.pin1
  N19: Pro_Mini_3V3_8MHz1.D6_PWM, IOL2.pin2
  N20: Pro_Mini_3V3_8MHz1.D5_PWM, IOL2.pin3
  N21: Pro_Mini_3V3_8MHz1.D4, IOL2.pin4
  N22: Pro_Mini_3V3_8MHz1.D3_PWM, IOL2.pin5
  N23: Pro_Mini_3V3_8MHz1.D2, IOL2.pin6
  N24: S2.pin0, S2.pin3, Power2.pin4
  N25: S2.pin2, S2.pin5, Power2.pin5
  N26: RTC3.INT, INT2.pin1, INT2.pin2, INT2.pin3, INT2.pin4, INT2.pin5, INT2.pin6, INT2.pin7, INT2.pin8, INT2.pin9, INT2.pin10, INT2.pin11, INT2.pin12, INT2.pin13, INT2.pin14, INT2.pin15
  N27: RTC3.GND, IOH4.pin4, Power4.pin6, Power4.pin7, BAT3.-
  N28: RTC3.SDA, AD4.pin5
  N29: RTC3.SCL, AD4.pin6
  N30: RTC3.VDD, D7.cathode, D8.cathode
  N31: S3.pin0, S3.pin3, Power4.pin5
  N32: S3.pin1, S3.pin4, D8.anode
  N33: S3.pin2, S3.pin5, Power4.pin4
  N34: D7.anode, BAT3.+
  N35: IOH4.pin5, J105.pin1
  N36: IOH4.pin6, J105.pin2
  N37: IOH4.pin7, J105.pin3
  N38: IOH4.pin8, J105.pin4
  N39: IOH4.pin9, J105.pin5
  N40: IOH4.pin10, J105.pin6
  N41: J105.pin8, IOL4.pin1
  N42: J105.pin9, IOL4.pin2
  N43: J105.pin10, IOL4.pin3
  N44: J105.pin11, IOL4.pin4
  N45: J105.pin12, IOL4.pin5
  N46: J105.pin13, IOL4.pin6
  N47: J105.pin14, IOL4.pin7
  N48: J105.pin15, IOL4.pin8
  N49: Xbee3.VCC, Power6.pin4
  N50: Xbee3.pin2, Tx4.pin1, Tx4.pin2, Tx4.pin3, Tx4.pin4, Tx4.pin5, Tx4.pin6, Tx4.pin7, Tx4.pin8, Tx4.pin9, Tx4.pin10, Tx4.pin11, Tx4.pin12, Tx4.pin13, Tx4.pin14, Tx4.pin15
  N51: Xbee3.pin3, Rx4.pin1, Rx4.pin2, Rx4.pin3, Rx4.pin4, Rx4.pin5, Rx4.pin6, Rx4.pin7, Rx4.pin8, Rx4.pin9, Rx4.pin10, Rx4.pin11, Rx4.pin12, Rx4.pin13, Rx4.pin14, Rx4.pin15
  N52: Xbee3.pin4, INT3.pin1, INT3.pin2, INT3.pin3, INT3.pin4, INT3.pin5, INT3.pin6, INT3.pin7, INT3.pin8, INT3.pin9, INT3.pin10, INT3.pin11, INT3.pin12, INT3.pin13, INT3.pin14, INT3.pin15
  N53: Xbee3.pin7, Power6.pin3
  N54: Xbee3.pin9, Sleep1.pin1, Sleep1.pin2, Sleep1.pin3, Sleep1.pin4, Sleep1.pin5, Sleep1.pin6, Sleep1.pin7, Sleep1.pin8, Sleep1.pin9, Sleep1.pin10, Sleep1.pin11
  N55: Xbee3.GND, IOH6.pin4, Power6.pin6, Power6.pin7
  N56: IOH6.pin5, J112.pin1, J113.pin1, J114.pin1
  N57: IOH6.pin6, J112.pin2, J113.pin2, J114.pin2
  N58: IOH6.pin7, J112.pin3, J113.pin3, J114.pin3
  N59: IOH6.pin8, J111.pin1, J112.pin4, J113.pin4, J114.pin4
  N60: IOH6.pin9, J111.pin2, J112.pin5, J113.pin5, J114.pin5
  N61: IOH6.pin10, J111.pin3, J112.pin6, J113.pin6, J114.pin6
  N62: J111.pin5, J112.pin8, J113.pin8, J114.pin8, IOL6.pin1
  N63: J111.pin6, J112.pin9, J113.pin9, J114.pin9, IOL6.pin2
  N64: J111.pin7, J112.pin10, J113.pin10, J114.pin10, IOL6.pin3
  N65: J111.pin8, J112.pin11, J113.pin11, J114.pin11, IOL6.pin4
  N66: J111.pin9, J112.pin12, J113.pin12, J114.pin12, IOL6.pin5
  N67: J111.pin10, J112.pin13, J113.pin13, J114.pin13, IOL6.pin6
  N68: J111.pin11, J112.pin14, J113.pin14, J114.pin14, IOL6.pin7
  N69: J112.pin15, J113.pin15, J114.pin15, IOL6.pin8

notes:
  もしくは

custom parts:
  Arduino Pro Mini v13: It's blue! It's thin! It's the Arduino Pro Mini! SparkFun's minimal design approach to Arduino. This is a 5V Arduino running the 16MHz bootloader. Arduino Pro Mini does not come with connectors populated so that you can solder in any connector or wire with any orientation you need. We recommend first time Arduino users start with the Uno R3. It's a great board that will get you up and running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
  Akizuki slide switch IS-1250: Akizuki slide switch is-1250 (P-01665)
  Power plug: 秋月電子通商 AE-DCJACK-DIPKIT-2.1mm-10A(通販コードK-06998)とその互換品(K06999,K-08415,K-08416)
  Arduino R3 6pin male header: Pin header for arduino R3
  RTC-8564NB: Real Time Clock Module and I2C-BUS interface method. This product is a module of the SON 8-pin DIP package. Supply voltage 1.8-5.5V original version by KimuShige
  SSCI-KIT-XBSOCKET: Xbee pin conversion
