# Fritzing sketch 5V昇圧DCDCシールド (saved by Fritzing 0.9.2b)
perfboards: 1

parts:
  IOL = female pin header, 8 pins [form="♀ (female)"]  # not connected
  IOH = female pin header, 10 pins [form="♀ (female)"]
  AD = female pin header, 6 pins [form="♀ (female)"]  # not connected
  POWER = female pin header, 8 pins [form="♀ (female)"]
  AE-MOD1 = AE-XCL101C501BR-G [part_number=AE-XCL101C501BR-G]

nets:
  GND: IOH.pin4, POWER.pin6, POWER.pin7, AE-MOD1.VSS
  N1: POWER.pin5, AE-MOD1.Vout
  VIN: POWER.pin8, AE-MOD1.Vbat, AE-MOD1.CE

custom parts:
  AE-XCL101C501BR-G: AE-XCL101C331BR-G
