# Fritzing sketch ArduinoProMini基板変換 (saved by Fritzing 0.9.2b)
perfboards: 1

parts:
  IOH = female pin header, 10 pins [form="♀ (female)"]
  IOL = female pin header, 8 pins [form="♀ (female)"]
  AD = female pin header, 6 pins [form="♀ (female)"]
  Power = female pin header, 8 pins [form="♀ (female)"]
  Reset = Momentary Switch [package=ksa_sealed_tac_switch]
  Pro_Mini_3V3_8MHz = Arduino Pro Mini v13
  S1 = Akizuki slide switch IS-1250
  Power_plug1 = Power plug
  J1 = Arduino R3 6pin male header [package=THT]  # not connected

nets:
  GND: IOH.pin4, Power.pin6, Power.pin7, Reset.4, Pro_Mini_3V3_8MHz.GND, Power_plug1.GND
  N1: IOH.pin5, Pro_Mini_3V3_8MHz.D13/SCK
  N2: IOH.pin6, Pro_Mini_3V3_8MHz.D12/MISO
  N3: IOH.pin7, Pro_Mini_3V3_8MHz.D11_PWM/MOSI
  N4: IOH.pin8, Pro_Mini_3V3_8MHz.D10_PWM/SS
  N5: IOH.pin9, Pro_Mini_3V3_8MHz.D9_PWM
  N6: IOH.pin10, Pro_Mini_3V3_8MHz.D8
  N7: IOL.pin1, Pro_Mini_3V3_8MHz.D7
  N8: IOL.pin2, Pro_Mini_3V3_8MHz.D6_PWM
  N9: IOL.pin3, Pro_Mini_3V3_8MHz.D5_PWM
  N10: IOL.pin4, Pro_Mini_3V3_8MHz.D4
  N11: IOL.pin5, Pro_Mini_3V3_8MHz.D3_PWM
  N12: IOL.pin6, Pro_Mini_3V3_8MHz.D2
  N13: IOL.pin7, Pro_Mini_3V3_8MHz.D1/RX
  N14: IOL.pin8, Pro_Mini_3V3_8MHz.D0/TX
  N15: AD.pin1, Pro_Mini_3V3_8MHz.A0
  N16: AD.pin2, Pro_Mini_3V3_8MHz.A1
  N17: AD.pin3, Pro_Mini_3V3_8MHz.A2
  N18: AD.pin4, Pro_Mini_3V3_8MHz.A3
  N19: AD.pin5, Pro_Mini_3V3_8MHz.A4
  N20: AD.pin6, Pro_Mini_3V3_8MHz.A5
  N21: Power.pin3, Reset.2, Pro_Mini_3V3_8MHz.RESET
  3V3: Power.pin4, S1.pin0, S1.pin3
  5V: Power.pin5, S1.pin2, S1.pin5
  RAW: Power.pin8, Pro_Mini_3V3_8MHz.RAW, Power_plug1.VCC
  VCC: Pro_Mini_3V3_8MHz.VCC, S1.pin1, S1.pin4

custom parts:
  Arduino Pro Mini v13: It's blue! It's thin! It's the Arduino Pro Mini! SparkFun's minimal design approach to Arduino. This is a 5V Arduino running the 16MHz bootloader. Arduino Pro Mini does not come with connectors populated so that you can solder in any connector or wire with any orientation you need. We recommend first time Arduino users start with the Uno R3. It's a great board that will get you up and running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
  Akizuki slide switch IS-1250: Akizuki slide switch is-1250 (P-01665)
  Power plug: 秋月電子通商 AE-DCJACK-DIPKIT-2.1mm-10A(通販コードK-06998)とその互換品(K06999,K-08415,K-08416)
  Arduino R3 6pin male header: Pin header for arduino R3
