# Fritzing sketch Xbeeシールド (saved by Fritzing 0.9.2b)
perfboards: 1

parts:
  IOH = female pin header, 10 pins [form="♀ (female)"]
  J1 = male pin header, 15 pins [form="♂ (male)"]
  IOL = female pin header, 8 pins [form="♀ (female)"]
  Power = female pin header, 8 pins [form="♀ (female)"]
  AD = female pin header, 6 pins [form="♀ (female)"]  # not connected
  INT = male pin header, 15 pins [form="♂ (male)"]
  J2 = male pin header, 15 pins [form="♂ (male)"]
  Tx = male pin header, 15 pins [form="♂ (male)"]
  J3 = male pin header, 15 pins [form="♂ (male)"]
  Rx = male pin header, 15 pins [form="♂ (male)"]
  Xbee1 = SSCI-KIT-XBSOCKET
  J4 = Arduino R3 6pin male header [package=THT]  # not connected
  Sleep = male pin header, 11 pins [form="♂ (male)"]
  J4_2 = male pin header, 11 pins [form="♂ (male)"]

nets:
  GND: IOH.pin4, Power.pin6, Power.pin7, Xbee1.GND
  N1: IOH.pin5, J1.pin1, J2.pin1, J3.pin1
  N2: IOH.pin6, J1.pin2, J2.pin2, J3.pin2
  N3: IOH.pin7, J1.pin3, J2.pin3, J3.pin3
  N4: IOH.pin8, J1.pin4, J2.pin4, J3.pin4, J4_2.pin1
  N5: IOH.pin9, J1.pin5, J2.pin5, J3.pin5, J4_2.pin2
  N6: IOH.pin10, J1.pin6, J2.pin6, J3.pin6, J4_2.pin3
  N7: J1.pin8, IOL.pin1, J2.pin8, J3.pin8, J4_2.pin5
  N8: J1.pin9, IOL.pin2, J2.pin9, J3.pin9, J4_2.pin6
  N9: J1.pin10, IOL.pin3, J2.pin10, J3.pin10, J4_2.pin7
  N10: J1.pin11, IOL.pin4, J2.pin11, J3.pin11, J4_2.pin8
  N11: J1.pin12, IOL.pin5, J2.pin12, J3.pin12, J4_2.pin9
  N12: J1.pin13, IOL.pin6, J2.pin13, J3.pin13, J4_2.pin10
  N13: J1.pin14, IOL.pin7, J2.pin14, J3.pin14, J4_2.pin11
  N14: J1.pin15, IOL.pin8, J2.pin15, J3.pin15
  RST: Power.pin3, Xbee1.pin7
  3.3V: Power.pin4, Xbee1.VCC
  INT: INT.pin1, INT.pin2, INT.pin3, INT.pin4, INT.pin5, INT.pin6, INT.pin7, INT.pin8, INT.pin9, INT.pin10, INT.pin11, INT.pin12, INT.pin13, INT.pin14, INT.pin15, Xbee1.pin4
  Tx: Tx.pin1, Tx.pin2, Tx.pin3, Tx.pin4, Tx.pin5, Tx.pin6, Tx.pin7, Tx.pin8, Tx.pin9, Tx.pin10, Tx.pin11, Tx.pin12, Tx.pin13, Tx.pin14, Tx.pin15, Xbee1.pin2
  Rx: Rx.pin1, Rx.pin2, Rx.pin3, Rx.pin4, Rx.pin5, Rx.pin6, Rx.pin7, Rx.pin8, Rx.pin9, Rx.pin10, Rx.pin11, Rx.pin12, Rx.pin13, Rx.pin14, Rx.pin15, Xbee1.pin3
  DTR/Sleep: Xbee1.pin9, Sleep.pin1, Sleep.pin2, Sleep.pin3, Sleep.pin4, Sleep.pin5, Sleep.pin6, Sleep.pin7, Sleep.pin8, Sleep.pin9, Sleep.pin10, Sleep.pin11

custom parts:
  SSCI-KIT-XBSOCKET: Xbee pin conversion
  Arduino R3 6pin male header: Pin header for arduino R3
