# Fritzing sketch grove3v3シールド (saved by Fritzing 0.9.2b)
perfboards: 1

parts:
  IOL = female pin header, 8 pins [form="♀ (female)"]
  IOH = female pin header, 10 pins [form="♀ (female)"]
  AD = female pin header, 6 pins [form="♀ (female)"]
  Power = female pin header, 8 pins [form="♀ (female)"]
  M-04522 = M-04522
  S1 = Akizuki slide switch IS-1250
  AD1 = Grove Header 4pin Straight direct mount [package=straight]
  AD2 = Grove Header 4pin Straight direct mount [package=straight]
  AD3 = Grove Header 4pin Straight direct mount [package=straight]
  AD4 = Grove Header 4pin Straight direct mount [package=straight]
  D1 = Grove Header 4pin Straight direct mount [package=straight]
  D2 = Grove Header 4pin Straight direct mount [package=straight]
  D3 = Grove Header 4pin Straight direct mount [package=straight]
  D4 = Grove Header 4pin Straight direct mount [package=straight]
  S2 = Akizuki slide switch IS-2235
  S3 = Akizuki slide switch IS-2235
  S4 = Akizuki slide switch IS-2235
  S5 = Akizuki slide switch IS-2235
  パーツ1 = Arduino Uno (Rev3)  # not connected
  S6 = Akizuki slide switch IS-2235
  S7 = Akizuki slide switch IS-2235
  S8 = Akizuki slide switch IS-2235
  S9 = Akizuki slide switch IS-2235
  J1 = male pin header, 15 pins [form="♂ (male)"]  # not connected
  J2 = male pin header, 15 pins [form="♂ (male)"]
  J3 = male pin header, 15 pins [form="♂ (male)"]  # not connected
  J4 = male pin header, 15 pins [form="♂ (male)"]
  J5 = male pin header, 15 pins [form="♂ (male)"]  # not connected
  J6 = male pin header, 15 pins [form="♂ (male)"]
  J7 = male pin header, 15 pins [form="♂ (male)"]  # not connected
  J8 = male pin header, 15 pins [form="♂ (male)"]

nets:
  A5: IOL.pin2
  A7: IOH.pin6
  A6: IOH.pin7
  N1: AD.pin1, S5.pin2, S5.pin4
  N2: AD.pin2, S4.pin2, S4.pin4
  N3: AD.pin3, S3.pin2, S3.pin4
  N4: AD.pin4, S2.pin2, S2.pin4
  3.3V: Power.pin4, M-04522.VCCA, S1.pin0, S1.pin3
  5V: Power.pin5, M-04522.VCCB
  GND: Power.pin7, AD1.1, AD2.1, AD3.1, AD4.1, D1.1, D2.1, D3.1, D4.1, S4.pin1
  N5: M-04522.A0, S5.pin3
  N6: M-04522.A1, S4.pin3
  N7: M-04522.A2, S3.pin3
  N8: M-04522.A3, S2.pin3
  A4: M-04522.A4, S9.pin5
  N9: M-04522.A5, S8.pin5
  N10: M-04522.A6, S6.pin5
  N11: M-04522.A7, S7.pin5
  N12: M-04522.GND, M-04522.OE
  A0/B0: M-04522.B0, S5.pin0
  A1/B1: M-04522.B1, S4.pin0
  A2/B2: M-04522.B2, S3.pin0
  A3/B3: M-04522.B3, S2.pin0
  N13: M-04522.B4, S9.pin2
  N14: M-04522.B5, S8.pin2
  N15: M-04522.B6, S6.pin2
  N16: M-04522.B7, S7.pin2
  VDD: S1.pin1, S1.pin4, AD1.2, AD2.2, AD3.2, AD4.2, D1.2, D2.2, D3.2, D4.2
  N17: S1.pin2, S1.pin5
  N18: AD1.3, AD2.4
  N19: AD1.4, S5.pin1
  N20: AD2.3, AD3.4, S3.pin1
  N21: AD3.3, AD4.4, S2.pin1
  B4: AD4.3, D1.4, S9.pin1
  B5: D1.3, D2.4, S8.pin1
  B6: D2.3, D3.4, S6.pin1
  B7: D3.3, D4.4, S7.pin1
  N22: S6.pin0, S6.pin4, J6.pin1
  N23: S7.pin0, S7.pin4, J8.pin1
  N24: S8.pin0, S8.pin4, J4.pin1
  N25: S9.pin0, S9.pin4, J2.pin1

custom parts:
  M-04522: Akizuki 8bit bi-directional logic level converter M-04522
  Akizuki slide switch IS-1250: Akizuki slide switch is-1250 (P-01665)
  Grove Header 4pin Straight direct mount: Header
  Akizuki slide switch IS-2235: Akizuki slide switch is-2235 (P-02627)
