# Fritzing sketch Xbeeホスト基板(昇圧電源) (saved by Fritzing 0.9.2b)
perfboards: 1

parts:
  Reset = Momentary Switch [package=ksa_sealed_tac_switch]
  Power_plug = AE-DC-POWER-JACK-DIP [part_number=AE-DC-POWER-JACK-DIP]
  Xbee = XBEE-1 [package=xbee-1]
  IOL = female pin header, 8 pins [form="♀ (female)"]
  IOH = female pin header, 10 pins [form="♀ (female)"]
  AD = female pin header, 6 pins [form="♀ (female)"]
  Power = female pin header, 8 pins [form="♀ (female)"]
  J1 = male pin header, 3 pins [form="♂ (male)"]
  R1 = Resistor [tolerance=±5% resistance=10k package=THT]
  Vol = Trimmer Potentiometer [maximum_resistance=0.1MΩ package=THT]
  AE-MOD1 = AE-XCL101C331BR-G [part_number=AE-XCL101C331BR-G]
  Power_plug1 = Power plug  # not connected

nets:
  N1: Reset.1, R1.Pin_0
  N2: Reset.2, Xbee.RESET, Power.pin3
  N3: Reset.3, Power_plug.GND#0, Power_plug.GND#2, Power.pin6, AE-MOD1.VSS
  N4: Power_plug.VCC#4, Power.pin8, AE-MOD1.Vbat, AE-MOD1.CE
  N5: Xbee.VDD, Power.pin4, R1.Pin_1, Vol.leg1, AE-MOD1.Vout
  N6: Xbee.DOUT, IOL.pin7
  N7: Xbee.DIN, IOL.pin8
  N8: Xbee.DIO12, IOH.pin6
  N9: Xbee.RSSI, IOH.pin8
  N10: Xbee.DIO11, IOH.pin7
  N11: Xbee.RES, J1.pin2
  N12: Xbee.DTR, IOH.pin10
  N13: Xbee.GND, IOH.pin4, Power.pin7, J1.pin3, Vol.leg2
  N14: Xbee.DIO4, IOL.pin4
  N15: Xbee.CTS, IOL.pin1
  N16: Xbee.DIO9, IOL.pin5
  N17: Xbee.DIO5, IOL.pin3
  N18: Xbee.RTS, IOL.pin2
  N19: Xbee.DIO3, AD.pin4
  N20: Xbee.DIO2, AD.pin3
  N21: Xbee.DIO1, AD.pin2
  N22: Xbee.DIO0, AD.pin1
  N23: J1.pin1, Vol.wiper

custom parts:
  AE-DC-POWER-JACK-DIP: 秋月電子通商 K-05148
